# Fritzing sketch Sketch_proto (saved by Fritzing 0.9.6b)

parts:
  Mod1 = Raspberry Pi 4B
  R3 = Resistor [tolerance=±5% power=0.25 resistance=220 package=THT]
  S1 = Pushbutton [package="[THT]"]
  LED1 = LED - 5mm [color="Red (633nm)" current=0.030 package="5 mm [THT]"]
  R1 = Resistor [tolerance=±5% power=0.25 resistance=220 package=THT]
  R4 = Resistor [tolerance=±5% power=0.25 resistance=220 package=THT]
  LED2 = LED - 5mm [color="Red (633nm)" current=0.030 package="5 mm [THT]"]
  U2 = L298_BRIDGE_DRIVER [package=powerso20]
  M1 = DC Motor  # not connected
  VCC2 = Battery block 9V  # not connected
  M2 = DC Motor

nets:
  N1: Mod1.GPIO18, LED1.anode
  N2: Mod1.GPIO23, LED2.anode
  N3: R3.Pin_1, S1.Pin_4
  N4: LED1.cathode, R1.Pin_1
  N5: R4.Pin_1, LED2.cathode
  N6: U2.IN3, M2.pin_2
  N7: U2.ENB, M2.pin_1
